// Logisim project WozBlaster - Direccionamiento MSX-OPL.circ as structural Verilog: 1 circuit, main circuit main
module main (
  input  A0,
  input  A1,
  input  A2,
  input  A3,
  input  A4,
  input  A5,
  input  A6,
  input  A7,
  input  nRD,
  input  nWR,
  input  nIORQ,
  input  nINT,
  input  nRESET,
  output OA0,
  output OA1,
  output OA2,
  output PCM,
  output out_18,
  output FM,
  output nBUSDIR,
  output out_21,
  output out_22,
  output nCS__OPL,
  output nIRQ__OPL,
  output nIC__OPL
);

  wire _3_out, _5_out, _7_out;

  and _5 (_5_out, A3, A4, A5);
  nor _3 (_3_out, A3, A4, A5);
  and _7 (_7_out, A2, A6);
  or _9 (nBUSDIR, nCS__OPL, nRD);
  or _10 (nCS__OPL, nIORQ, out_18);
  xnor _1 (OA1, A1, A7);
  and _4 (PCM, OA2, _7_out, _5_out);
  and _6 (FM, _3_out, _7_out, A7);
  not _8 (OA2, A7);
  nor _2 (out_18, PCM, FM);

  assign nIC__OPL = nRESET;
  assign nIRQ__OPL = nINT;
  assign OA0 = A0;
  assign out_21 = nRD;
  assign out_22 = nWR;

  // Notes on the sheet:
  //   A2: pull=up
endmodule
